# Fritzing sketch Hexapod MK2 Wiring Diagram (saved by Fritzing 0.9.4)

parts:
  9G_Servo_hip = Basic Servo
  NodeMCU_V2 = NodeMCU V1.0
  MPU_6050 = InvenSense MPU6050
  3S_11_1V_2200mAh_LiPo = LiPoly Battery (1300mAh)
  Mini_360 = Mini-360 DC-DC Buck converter [package=THT]
  Mini_360_2 = Mini-360 DC-DC Buck converter [package=THT]
  Mini_360_3 = Mini-360 DC-DC Buck converter [package=THT]
  PCA_9685 = PCA9685 16x12-bit PWM Breakout
  9G_Servo_knee = Basic Servo
  9G_Servo_foot = Basic Servo
  9G_Servo_hip_2 = Basic Servo
  9G_Servo_knee_2 = Basic Servo
  9G_Servo_foot_2 = Basic Servo
  9G_Servo_hip_3 = Basic Servo
  9G_Servo_knee_3 = Basic Servo
  9G_Servo_foot_3 = Basic Servo
  9G_Servo_knee_4 = Basic Servo
  9G_Servo_hip_4 = Basic Servo
  9G_Servo_knee_5 = Basic Servo
  9G_Servo_hip_5 = Basic Servo
  9G_Servo_hip_6 = Basic Servo
  9G_Servo_foot_4 = Basic Servo
  9G_Servo_foot_5 = Basic Servo
  9G_Servo_knee_6 = Basic Servo
  9G_Servo_foot_6 = Basic Servo
  Mini_360_4 = Mini-360 DC-DC Buck converter [package=THT]
  Bauteil1 = NRF24L01+ Breakout Board

nets:
  GND: 9G_Servo_hip.gnd, 9G_Servo_knee.gnd, 9G_Servo_foot.gnd, 9G_Servo_hip_4.gnd, 9G_Servo_foot_5.gnd, 9G_Servo_knee_6.gnd, Mini_360_4.OUT-
  VCC: 9G_Servo_hip.vcc, 9G_Servo_knee.vcc, 9G_Servo_foot.vcc, 9G_Servo_hip_4.vcc, 9G_Servo_foot_5.vcc, 9G_Servo_knee_6.vcc, Mini_360_4.OUT+
  N1: 9G_Servo_hip.pulse, PCA_9685.no_name_yet#7
  N2: NodeMCU_V2.D0, Bauteil1.CS
  N3: NodeMCU_V2.D1, MPU_6050.SCL, PCA_9685.no_name_yet#503, PCA_9685.no_name_yet#603
  N4: NodeMCU_V2.D2, MPU_6050.SDA, PCA_9685.no_name_yet#504, PCA_9685.no_name_yet#604
  N5: NodeMCU_V2.D3, 9G_Servo_foot_6.pulse
  N6: NodeMCU_V2.D4, Bauteil1.CE
  3V3: NodeMCU_V2.3V3, Bauteil1.VCC
  GND_2: NodeMCU_V2.GND, MPU_6050.GND, Mini_360_3.OUT-, PCA_9685.no_name_yet#501, Bauteil1.GND
  N7: NodeMCU_V2.D5, Bauteil1.SCK
  N8: NodeMCU_V2.D6, Bauteil1.MISO
  N9: NodeMCU_V2.D7, Bauteil1.MOSI
  N10: NodeMCU_V2.D8, 9G_Servo_foot_3.pulse
  VIN: NodeMCU_V2.Vin, MPU_6050.VCC, Mini_360_3.OUT+, PCA_9685.no_name_yet#505
  N11: 3S_11_1V_2200mAh_LiPo.positive, Mini_360.IN+, Mini_360_2.IN+, Mini_360_3.IN+, Mini_360_4.IN+
  N12: 3S_11_1V_2200mAh_LiPo.negative, Mini_360.IN-, Mini_360_2.IN-, Mini_360_3.IN-, Mini_360_4.IN-
  VCC_2: Mini_360.OUT+, 9G_Servo_hip_2.vcc, 9G_Servo_knee_2.vcc, 9G_Servo_foot_2.vcc, 9G_Servo_knee_5.vcc, 9G_Servo_hip_6.vcc, 9G_Servo_foot_4.vcc
  GND_3: Mini_360.OUT-, 9G_Servo_hip_2.gnd, 9G_Servo_knee_2.gnd, 9G_Servo_foot_2.gnd, 9G_Servo_knee_5.gnd, 9G_Servo_hip_6.gnd, 9G_Servo_foot_4.gnd
  VCC_3: Mini_360_2.OUT+, 9G_Servo_hip_3.vcc, 9G_Servo_knee_3.vcc, 9G_Servo_foot_3.vcc, 9G_Servo_knee_4.vcc, 9G_Servo_hip_5.vcc, 9G_Servo_foot_6.vcc
  GND_4: Mini_360_2.OUT-, 9G_Servo_hip_3.gnd, 9G_Servo_knee_3.gnd, 9G_Servo_foot_3.gnd, 9G_Servo_knee_4.gnd, 9G_Servo_hip_5.gnd, 9G_Servo_foot_6.gnd
  N13: PCA_9685.no_name_yet#0, 9G_Servo_knee_3.pulse
  N14: PCA_9685.no_name_yet#1, 9G_Servo_hip_3.pulse
  N15: PCA_9685.no_name_yet#2, 9G_Servo_foot_2.pulse
  N16: PCA_9685.no_name_yet#3, 9G_Servo_knee_2.pulse
  N17: PCA_9685.no_name_yet#4, 9G_Servo_hip_2.pulse
  N18: PCA_9685.no_name_yet#5, 9G_Servo_foot.pulse
  N19: PCA_9685.no_name_yet#6, 9G_Servo_knee.pulse
  N20: PCA_9685.no_name_yet#8, 9G_Servo_hip_4.pulse
  N21: PCA_9685.no_name_yet#9, 9G_Servo_knee_6.pulse
  N22: PCA_9685.no_name_yet#10, 9G_Servo_foot_5.pulse
  N23: PCA_9685.no_name_yet#11, 9G_Servo_hip_6.pulse
  N24: PCA_9685.no_name_yet#12, 9G_Servo_knee_5.pulse
  N25: PCA_9685.no_name_yet#13, 9G_Servo_foot_4.pulse
  N26: PCA_9685.no_name_yet#14, 9G_Servo_hip_5.pulse
  N27: PCA_9685.no_name_yet#15, 9G_Servo_knee_4.pulse

notes:
  back left
  middle left
  front left
  front right
  back right
  middle right

custom parts:
  NodeMCU V1.0: ESP8266 based NodeMCU
  LiPoly Battery (1300mAh): Lithium Ion Polymer Battery (1300mAh)
  Mini-360 DC-DC Buck converter: Mini-360 DC-DC Buck converter. Tiny buck step down voltage converter, input voltage 4.75 to 23V output 1 to 17V adjustable. Available from ebay and the like.
